# Fritzing sketch CircuitDiagram_old (saved by Fritzing 0.9.2b)
breadboards: 1

parts:
  Part1 = Arduino Uno (Rev3)
  LCD1 = LCD screen
  IR1 = TSOP312.., 314.. [package=THT]
  U1 = POT [package=alps_pot]
  S1 = Pushbutton [package="[SMD]"]
  R1 = Resistor [tolerance=±5% resistance=220 package="0805 [SMD]"]
  S2 = Pushbutton [package="[SMD]"]
  R2 = Resistor [tolerance=±5% resistance=220 package="0805 [SMD]"]
  J1 = Piezo Speaker

nets:
  N1: Part1.A0, U1.S
  N2: Part1.D8, LCD1.E
  N3: Part1.D9_PWM, LCD1.RS
  N4: Part1.D12/MISO, IR1.Data
  N5: Part1.D13/SCK, J1.pin2
  GND: Part1.GND, LCD1.VSS, LCD1.V0, LCD1.R/W, LCD1.LED-, IR1.GND, U1.E, R1.Pin_0, J1.pin1
  N6: Part1.D2, S2.Pin_3, S2.Pin_4, R2.Pin_1
  N7: Part1.D3_PWM, S1.Pin_3, S1.Pin_4, R1.Pin_1
  N8: Part1.D4, LCD1.DB7
  N9: Part1.D5_PWM, LCD1.DB6
  N10: Part1.D6_PWM, LCD1.DB5
  N11: Part1.D7, LCD1.DB4
  5V: Part1.5V, LCD1.VDD, LCD1.LED+, IR1.Vs, U1.A, S1.Pin_1, S1.Pin_2, S2.Pin_1, S2.Pin_2, R2.Pin_0
